# Fritzing sketch dmdschematic (saved by Fritzing 1.0.0rc)
breadboards: 1

parts:
  WeMos_D1_Mini1 = WeMos D1 Mini
  R1 = Resistor [tolerance=±5% power=0.25W resistance=10k package=THT]
  IC1 = IC, DIP package, 16 pins [chip_label=IC]
  S2 = Pushbutton [package="[THT]"]

nets:
  N1: WeMos_D1_Mini1.5V, S2.Pin_1, S2.Pin_2
  N2: WeMos_D1_Mini1.D0, IC1.pin16
  N3: WeMos_D1_Mini1.D2, R1.Pin_1, S2.Pin_3, S2.Pin_4
  N4: WeMos_D1_Mini1.D3, IC1.pin12
  N5: WeMos_D1_Mini1.D5, IC1.pin13
  N6: WeMos_D1_Mini1.D6, IC1.pin15
  N7: WeMos_D1_Mini1.D7, IC1.pin11
  N8: WeMos_D1_Mini1.D8, IC1.pin1
  N9: WeMos_D1_Mini1.G, R1.Pin_0, IC1.pin2, IC1.pin3, IC1.pin4, IC1.pin5, IC1.pin6, IC1.pin7, IC1.pin8
